# Fritzing sketch organicemos (saved by Fritzing 0.9.3b)

parts:
  Componente1 = Arduino Nano (Rev3.0)
  Componente2 = MPR121 Breakout
  Componente3 = MPR121 Breakout
  Componente4 = MPR121 Breakout
  U1 = WS2812 RGB LED strip
  R1 = Resistor [tolerance=±5% resistance=470 package="2010 [SMD]"]
  J1 = Power Jack [package=power_jack_combo]
  U2 = Mini-USB _B_ connector with 5th pin broken out. [package=usb-minib]  # not connected

nets:
  GND: Componente1.GND, Componente2.GND, Componente3.GND, Componente4.GND, U1.GND, J1.GND
  N1: Componente1.D2, Componente2.~IRQ, Componente3.~IRQ, Componente4.~IRQ
  N2: Componente1.D8, R1.Pin_1
  N3: Componente1.A5, Componente2.SCL, Componente3.SCL, Componente4.SCL
  N4: Componente1.A4, Componente2.SDA, Componente3.SDA, Componente4.SDA
  3.3V: Componente1.3V3, Componente2.3.3V, Componente3.ADDR, Componente3.3.3V, Componente4.3.3V
  N5: U1.VCC, J1.PWR
  N6: U1.DIN, R1.Pin_0

custom parts:
  WS2812 RGB LED strip: WS2812 strip
